// Logisim project 7 SEGMENTOS.circ as structural Verilog: 2 circuits, main circuit 7SEG
module _7SEG (
  input  A,
  input  B,
  input  C,
  input  D,
  output A_2,
  output B_2,
  output C_2,
  output D_2,
  output E,
  output F,
  output G
);

  wire and_1_out, and_2_out, and_3_out, and_4_out, and_5_out, and_6_out, and_7_out, and_8_out, and_9_out,
       and_10_out, and_11_out, and_12_out, xnor_1_out, xnor_2_out;

  xnor xnor_1 (xnor_1_out, B, D);
  xnor xnor_2 (xnor_2_out, C, D);
  or or_1 (C_2, B, ~C, D);  // OR_Gate
  and and_1 (and_1_out, ~B, ~D);  // AND_Gate
  and and_2 (and_2_out, ~B, C);  // AND_Gate
  and and_3 (and_3_out, C, ~D);  // AND_Gate
  and and_4 (and_4_out, B, ~C, D);  // AND_Gate
  and and_5 (and_5_out, ~B, ~D);  // AND_Gate
  and and_6 (and_6_out, C, ~D);  // AND_Gate
  and and_7 (and_7_out, ~C, ~D);  // AND_Gate
  and and_8 (and_8_out, B, ~C);  // AND_Gate
  and and_9 (and_9_out, B, ~D);  // AND_Gate
  and and_10 (and_10_out, B, ~C);  // AND_Gate
  and and_11 (and_11_out, ~B, C);  // AND_Gate
  and and_12 (and_12_out, C, ~D);  // AND_Gate
  or or_2 (A_2, A, C, xnor_1_out);
  or or_3 (B_2, ~B, xnor_2_out);  // OR_Gate
  or or_4 (E, and_5_out, and_6_out);
  or or_5 (G, A, and_10_out, and_11_out, and_12_out);
  or or_6 (D_2, A, and_1_out, and_2_out, and_3_out, and_4_out);
  or or_7 (F, A, and_7_out, and_8_out, and_9_out);
endmodule

module display (
  input  in_1,
  input  in_2,
  input  in_3,
  input  in_4
);

  wire n7seg_1_a_2, n7seg_1_b_2, n7seg_1_c_2, n7seg_1_d_2, n7seg_1_e, n7seg_1_f, n7seg_1_g;

  _7SEG u_7seg_1 (
    .A(in_1), .B(in_2), .C(in_3), .D(in_4), .A_2(n7seg_1_a_2), .B_2(n7seg_1_b_2), .C_2(n7seg_1_c_2),
    .D_2(n7seg_1_d_2), .E(n7seg_1_e), .F(n7seg_1_f), .G(n7seg_1_g));
  _7_Segment_Display u_7_segment_display_1 (
    .g(n7seg_1_g), .f(n7seg_1_f), .a(n7seg_1_a_2), .b(n7seg_1_b_2), .e(n7seg_1_e), .d(n7seg_1_d_2),
    .c(n7seg_1_c_2));  // open: dp
endmodule
